// Logisim project lab4.circ as structural Verilog: 1 circuit, main circuit main
module main (
  output Red,
  output Yellow,
  output Green
);

  wire _08_2_out, _08_3_out, _08_out, _32_out, and_1_out, and_2_out, clock_1_out, D0_q, D0_qn, D1_qn, D2_q,
       D2_qn;

  Clock clock_1 (.out(clock_1_out));
  D_Flip_Flop D2 (.clk(clock_1_out), .D(_08_out), .Q(D2_q), .Qn(D2_qn));  // open: preset, en, reset
  and _08 (_08_out, _08_2_out, Red);
  and _08_2 (_08_2_out, D2_qn, D0_qn);
  D_Flip_Flop D1 (.clk(clock_1_out), .D(_08_3_out), .Q(Red), .Qn(D1_qn));  // open: preset, en, reset
  D_Flip_Flop D0 (.clk(clock_1_out), .D(D1_qn), .Q(D0_q), .Qn(D0_qn));  // open: preset, en, reset
  or _32 (_32_out, Red, D0_q);
  and _08_3 (_08_3_out, D2_qn, _32_out);
  and and_1 (and_1_out, D2_q, Red);
  nor nor_1 (Green, D2_q, Red, D0_q);
  and and_2 (and_2_out, D0_q, D1_qn);
  or or_1 (Yellow, and_1_out, and_2_out);

  // Notes on the sheet:
  //   11
  //   12
  //   5
  //   3
  //   2
  //   6
  //   8
  //   11
  //   13
  //   12
  //   9
  //   8
  //   9
  //   10
endmodule
